# Fritzing sketch ESP_Double_box_switch (saved by Fritzing 0.9.3b)
circuit board: 6.37583cm x 4.41212cm

parts:
  JP1 = Header 2 [package=molex-1x2_lock]
  D1 = Diode [package=diode-1n4001]
  Q1 = PNP-Transistor [package="TO92 [THT]"]
  POWER_2 = LED - 5mm [color="Red (633nm)" package="5 mm [THT]"]
  Relay2 = OMRON PCB Power Relay – G5LE [part_number="G5LE-1\n" package=THT]
  Relay2_R_TO_MC = Resistor [tolerance=±5% resistance=1k package=THT]
  RELAY2_R_5V = Resistor [tolerance=±5% resistance=1k package=THT]
  JP3 = Header 2 [package=molex-1x2_lock]
  RELAY1_R_5V = Resistor [tolerance=±5% resistance=1k package=THT]
  Relay1_R_TO_MC = Resistor [tolerance=±5% resistance=1k package=THT]
  D2 = Diode [package=diode-1n4001]
  Q2 = PNP-Transistor [package="TO92 [THT]"]
  MQTT_CONN = LED - 5mm [color="Red (633nm)" package="5 mm [THT]"]
  Espessif_Serial_Wifi_Modul_1 = ESP8266 ESP01 [part_number=ESP8266 package=THT]
  R5 = Resistor [tolerance=±5% resistance=220 package=THT]
  RESET = Momentary Switch [package=ksa_sealed_tac_switch]
  R6 = Resistor [tolerance=±5% resistance=220 package=THT]
  R7 = Resistor [tolerance=±5% resistance=220 package=THT]
  R8 = Resistor [tolerance=±5% resistance=220 package=THT]
  R9 = Resistor [tolerance=±5% resistance=220 package=THT]
  Relay1 = OMRON PCB Power Relay – G5LE [part_number="G5LE-1\n" package=THT]
  JP2 = Header 2 [package=molex-1x2_lock]

nets:
  N1: JP1.1, Relay2.C
  N2: JP1.2, Relay2.A
  N3: D1.A, Q1.C, POWER_2.cathode, POWER_2.anode, Relay2.COIL1, RELAY2_R_5V.Pin_1
  N4: D1.C, Relay2.COIL2, RELAY2_R_5V.Pin_0, RELAY1_R_5V.Pin_0, D2.C, MQTT_CONN.anode, Espessif_Serial_Wifi_Modul_1.VCC, Espessif_Serial_Wifi_Modul_1.CH_PD, R5.Pin_0, R6.Pin_0, R7.Pin_0, Relay1.COIL2, JP2.1
  N5: Q1.E, Q2.E, Espessif_Serial_Wifi_Modul_1.GND, RESET.3, R8.Pin_0, R9.Pin_0, JP2.2
  N6: Q1.B, Relay2_R_TO_MC.Pin_1
  N7: Relay2_R_TO_MC.Pin_0, Espessif_Serial_Wifi_Modul_1.TXD, R8.Pin_1
  N8: JP3.1, Relay1.C
  N9: JP3.2, Relay1.A
  N10: RELAY1_R_5V.Pin_1, D2.A, Q2.C, Relay1.COIL1
  N11: Relay1_R_TO_MC.Pin_0, Espessif_Serial_Wifi_Modul_1.RXD, R9.Pin_1
  N12: Relay1_R_TO_MC.Pin_1, Q2.B
  N13: MQTT_CONN.cathode, Espessif_Serial_Wifi_Modul_1.GPIO00, R6.Pin_1
  N14: Espessif_Serial_Wifi_Modul_1.GPIO16, R5.Pin_1, RESET.1
  N15: Espessif_Serial_Wifi_Modul_1.GPIO02, R7.Pin_1

custom parts:
  ESP8266 ESP01: Generic WiFi Module based on the ESP8266 with onboard PCB antenna and UART communications
